# Fritzing sketch RepRepDiscount (saved by Fritzing 0.9.4)

parts:
  J1 = shrouded pin header, 10 pins [form="♂ (shrouded male)"]
  J2 = shrouded pin header, 10 pins [form="♂ (shrouded male)"]
  J3 = female pin header, 5 pins [form="♀ (female)"]
  J4 = female pin header, 5 pins [form="♀ (female)"]
  J3_2 = female pin header, 5 pins [form="♀ (female)"]
  J5 = female pin header, 5 pins [form="♀ (female)"]

nets:
  N1: J1.pin1, J5.pin1
  N2: J1.pin2, J5.pin2
  N3: J1.pin3, J5.pin3
  N4: J1.pin4, J5.pin4
  N5: J1.pin5, J5.pin5
  N6: J1.pin6, J3_2.pin5
  N7: J1.pin7, J3_2.pin4
  N8: J1.pin8, J3_2.pin3
  N9: J1.pin9, J3_2.pin2
  N10: J1.pin10, J3_2.pin1
  N11: J2.pin1, J3.pin1
  N12: J2.pin2, J3.pin2
  N13: J2.pin3, J3.pin3
  N14: J2.pin4, J3.pin4
  N15: J2.pin7, J4.pin4
  N16: J2.pin8, J4.pin3
  N17: J2.pin9, J4.pin2
  N18: J2.pin10, J4.pin1

notes:
  Pin number labels on the PCB are often bonkers (and sometimes the connector has been inserted upside down!), so go by position, as viewed from the back of the board, as below:
  Exp1:
  Enc.Sw | RS | D5 | D7 | 5V
  Grey | Yellow | White| White| Red
  -------------------------------------------------
  Buzzer | Enable | D4 | D6 | GND
  Purple | Blue | White |White| Black
  Exp2:
  CLK | CS/SS | DIn (MOSI | Btn | NC
  Yellow | White | Blue | Grey | -
  ----------------------------------------------------
  DOut (MISO) | Enc.A | Enc.B | SD DETECT | NC
  Green | Yellow | Yellow | Brown | -
  https://forum.arduino.cc/t/how-to-use-reprapdiscount-smart-controller/535246/27
