# Fritzing sketch LCD12864 Wiring (saved by Fritzing 0.9.3b)

parts:
  GLCD_128x1 = 128 x 64 Graphic LCD
  R1 = Resistor [tolerance=±5% resistance=220 package=THT]
  R2 = Rotary Potentiometer (Large) [maximum_resistance=100kΩ package=THT]
  J1 = female pin header, 6 pins [form="♀ (female)"]

nets:
  N1: GLCD_128x1.1_Vss, GLCD_128x1.15_CS1, GLCD_128x1.20_K(-), R2.leg2, J1.pin2
  N2: GLCD_128x1.2_Vdd, R1.Pin_1, R2.leg1, J1.pin1
  N3: GLCD_128x1.3_Vo, R2.wiper
  N4: GLCD_128x1.4_D/I, J1.pin5
  N5: GLCD_128x1.5_R/W, J1.pin4
  N6: GLCD_128x1.6_Enable, J1.pin3
  N7: GLCD_128x1.17_RST, J1.pin6
  N8: GLCD_128x1.19_A(+), R1.Pin_0

notes:
  10k linear pot (optional) allows adjustable contrast
